# Fritzing sketch iago-exercise-001 (saved by Fritzing 0.9.3b)
breadboards: 1

parts:
  Part1 = Arduino Uno (Rev3) - ICSP
  R1 = Resistor [tolerance=±5% resistance=150 package=THT]
  LED1 = smd LED [color="Blue (505nm)" package="0805 [SMD]"]

nets:
  N1: Part1.GND, LED1.cathode
  N2: Part1.D2, R1.Pin_0
  N3: R1.Pin_1, LED1.anode
